# Fritzing sketch diagram (saved by Fritzing 0.9.4)
breadboards: 1

parts:
  Part1 = Arduino Nano (Rev3.0)
  J1 = Basic Servo
  HC-SR04_Sensor_1 = HC-SR04 Ultrasonic Distance Sensor

nets:
  GND: Part1.GND, J1.gnd, HC-SR04_Sensor_1.GND
  N1: Part1.D2, J1.pulse
  VCC: Part1.5V, J1.vcc, HC-SR04_Sensor_1.VCC
  N2: Part1.A7, HC-SR04_Sensor_1.TRIG
  N3: Part1.A6, HC-SR04_Sensor_1.ECHO
